# Fritzing sketch LDR (saved by Fritzing 0.9.3b)
breadboards: 1

parts:
  R1 = Photocell (LDR) [package=THT]
  R2 = Resistor [tolerance=±5% resistance=10k package=THT]
  Part1 = Arduino Uno (Rev3)

nets:
  N1: R1.pin_0, R2.Pin_1, Part1.A5/SCL
  N2: R1.pin_1, Part1.5V
  N3: R2.Pin_0, Part1.GND
